# Fritzing sketch Esquema Fritzing (saved by Fritzing 0.9.3b)
breadboards: 2

parts:
  IC1 = ULN2003A [package="SO16 [SMD]"]
  M1 = Stepper Motor - Unipolar
  J1 = Basic Servo
  J2 = Basic Servo
  J3 = Basic Servo
  J4 = Basic Servo
  Componente2 = Arduino Uno (Rev3)
  LCD1 = LCD screen  # not connected
  S1 = Pushbutton [package=THT]
  R1 = Resistor [tolerance=±5% resistance=220 package=THT]
  R2 = Resistor [tolerance=±5% resistance=1k package=THT]
  R3 = Resistor [tolerance=±5% resistance=220 package=THT]
  J5 = Piezo Speaker
  LED1 = LED - 3mm [color="Red (633nm)" package="3 mm [THT]"]
  LED2 = LED - 3mm [color="Green (555nm)" package="3 mm [THT]"]

nets:
  N1: IC1.In_1, Componente2.D13/SCK
  N2: IC1.In_2, Componente2.D12/MISO
  N3: IC1.In_3, Componente2.D11_PWM/MOSI
  VCC: IC1.0V, J1.vcc, J2.vcc, J3.vcc, J4.vcc, Componente2.5V, R2.Pin_0
  GND: IC1.COM_-_Common, M1.C, M1.D, J1.gnd, J2.gnd, J3.gnd, Componente2.GND, S1.leg0, R1.Pin_1, R3.Pin_1, J5.pin1, LED1.cathode, LED1.anode, LED2.cathode, LED2.anode
  N4: IC1.Out_4, M1.COMMON_2
  N5: IC1.Out_2, M1.COMMON_1
  N6: J1.pulse, Componente2.D7
  N7: J2.pulse, Componente2.D9_PWM
  N8: J3.pulse, Componente2.D6_PWM
  N9: J4.pulse, Componente2.D8
  N10: Componente2.D2, S1.leg1, R2.Pin_1
  N11: Componente2.D3_PWM, R3.Pin_0
  N12: Componente2.D4, R1.Pin_0
  N13: Componente2.D5_PWM, J5.pin2
